// Logisim project bcd.circ as structural Verilog: 1 circuit, main circuit implementation
module implementation (
  input  w3,
  input  w2,
  input  w1,
  input  w0,
  output a,
  output b,
  output c,
  output d,
  output e,
  output f,
  output g
);

  wire and_1_out, and_3_out, and_4_out, and_6_out, and_7_out, and_8_out, and_9_out, and_10_out, and_11_out,
       and_12_out, and_13_out, and_14_out, and_15_out, and_16_out, N102_OR_3, not_1_out, not_2_out,
       not_3_out, not_4_out, not_5_out, not_6_out, not_7_out, not_8_out, not_9_out, not_10_out, not_11_out,
       not_12_out, not_13_out, not_14_out, not_15_out, not_16_out, not_17_out, not_18_out, not_19_out,
       not_20_out, not_21_out, Nw0_A_Nw2_OR_Nw2_A_w1, Nw2_OR_Nw0_AND_Nw1, or_4_out, or_5_out, or_6_out,
       or_7_out, or_8_out, or_9_out, w0_AND_w1, w1_AND_Nw0;

  not not_1 (not_1_out, w0);
  not not_2 (not_2_out, w1);
  not not_3 (not_3_out, w2);
  and and_1 (and_1_out, not_1_out, not_2_out);
  and and_2 (w0_AND_w1, w0, w1);
  not not_4 (not_4_out, w0);
  not not_5 (not_5_out, w2);
  not not_6 (not_6_out, w2);
  not not_7 (not_7_out, w0);
  not not_8 (not_8_out, w1);
  or or_1 (Nw2_OR_Nw0_AND_Nw1, not_3_out, and_1_out);
  and and_3 (and_3_out, not_4_out, not_5_out);
  and and_4 (and_4_out, not_6_out, w1);
  and and_5 (w1_AND_Nw0, w1, not_7_out);
  and and_6 (and_6_out, w2, w0, not_8_out);
  not not_9 (not_9_out, w2);
  not not_10 (not_10_out, w0);
  or or_2 (Nw0_A_Nw2_OR_Nw2_A_w1, and_3_out, and_4_out);
  or or_3 (N102_OR_3, and_6_out, w3);
  and and_7 (and_7_out, not_9_out, not_10_out);
  and and_8 (and_8_out, w2, w0);
  or or_4 (or_4_out, and_8_out, w3);
  not not_11 (not_11_out, w1);
  // Probe on or_5_out
  or or_5 (or_5_out, and_7_out, w1);
  or or_6 (or_6_out, not_11_out, w0);
  or or_7 (or_7_out, Nw0_A_Nw2_OR_Nw2_A_w1, w1_AND_Nw0);
  // Probe on a
  or a_OR (a, or_5_out, or_4_out);
  // Probe on b
  or b_OR (b, Nw2_OR_Nw0_AND_Nw1, w0_AND_w1);
  // Probe on c
  or c_OR (c, w2, or_6_out);
  // Probe on d
  or d_OR (d, or_7_out, N102_OR_3);
  not not_12 (not_12_out, w0);
  not not_13 (not_13_out, w2);
  not not_14 (not_14_out, w0);
  not not_15 (not_15_out, w0);
  not not_16 (not_16_out, w1);
  not not_17 (not_17_out, w0);
  and and_9 (and_9_out, not_12_out, not_13_out);
  and and_10 (and_10_out, w1, not_14_out);
  and and_11 (and_11_out, not_15_out, not_16_out);
  and and_12 (and_12_out, w2, not_17_out);
  and and_13 (and_13_out, w2, not_18_out);
  not not_18 (not_18_out, w1);
  and and_14 (and_14_out, w1, not_19_out);
  not not_19 (not_19_out, w2);
  and and_15 (and_15_out, w1, not_20_out);
  not not_20 (not_20_out, w0);
  not not_21 (not_21_out, w1);
  and and_16 (and_16_out, not_21_out, w2);
  or e_OR (e, and_9_out, and_10_out);
  or or_8 (or_8_out, and_11_out, and_12_out);
  or f_OR (f, or_8_out, or_9_out);
  or or_9 (or_9_out, and_13_out, w3);
  or g_OR (g, and_14_out, and_15_out, and_16_out, w3);

  // Other names for the same wires on the sheet: at = a; bt = b; ct = c; dt = d; et = e; ft = f; gt = g; w0t = w0;
  //   w1t = w1; w2t = w2; w3t = w3
endmodule
