// Logisim project grey.circ as structural Verilog: 1 circuit, main circuit implementation
module implementation (
  input  x2,
  input  x1,
  input  x0,
  output y2,
  output y1,
  output y0
);

  xor xor_1 (y1, x1, x2);
  xor xor_2 (y0, x0, x1);

  assign y2 = x2;

  // Other names for the same wires on the sheet: x0t = x0; x1t = x1; y0t = y0; y1t = y1; x2t = x2; y2t = x2
endmodule
