// Logisim project adder4.circ as structural Verilog: 1 circuit, main circuit implementation
module implementation (
  input  [3:0] Ain,
  input  [3:0] Bin,
  input  Cinin,
  output [3:0] Sum_Out,
  output Carry_Out
);

  wire and_1_out, and_2_out, and_3_out, and_4_out, and_5_out, and_6_out, and_7_out, and_8_out, and_9_out,
       and_10_out, and_11_out, and_12_out, and_13_out, and_14_out, buffer_1_out, buffer_2_out, buffer_3_out,
       buffer_4_out, buffer_5_out, buffer_6_out, buffer_7_out, buffer_8_out, buffer_9_out, buffer_10_out,
       NAND1, NAND2, NAND3, NAND4, Ncin, NOR1, NOR2, NOR3, NOR4, nor_5_out, nor_6_out, nor_7_out, nor_8_out,
       not_2_out, xor_1_out, xor_2_out, xor_3_out, xor_4_out;

  buf buffer_1 (buffer_1_out, Ain[0]);
  buf buffer_2 (buffer_2_out, Bin[0]);
  buf buffer_3 (buffer_3_out, Ain[2]);
  buf buffer_4 (buffer_4_out, Bin[2]);
  buf buffer_5 (buffer_5_out, Ain[3]);
  buf buffer_6 (buffer_6_out, Bin[3]);
  not not_1 (Ncin, Cinin);
  nor nor_1 (NOR1, buffer_1_out, buffer_2_out);
  nand nand_1 (NAND1, buffer_2_out, buffer_1_out);
  nor nor_2 (NOR2, Ain[1], Bin[1]);
  nand nand_2 (NAND2, Ain[1], Bin[1]);
  nor nor_3 (NOR3, buffer_3_out, buffer_4_out);
  nand nand_3 (NAND3, buffer_3_out, buffer_4_out);
  nor nor_4 (NOR4, buffer_5_out, buffer_6_out);
  nand nand_4 (NAND4, buffer_5_out, buffer_6_out);
  not not_2 (not_2_out, Ncin);
  and and_1 (and_1_out, ~NOR1, NAND1);  // AND_Gate
  and and_2 (and_2_out, NAND1, Ncin);
  buf buffer_7 (buffer_7_out, NOR1);
  and and_3 (and_3_out, ~NOR2, NAND2);  // AND_Gate
  and and_4 (and_4_out, Ncin, NAND1, NAND2);
  and and_5 (and_5_out, NAND2, NOR1);
  buf buffer_8 (buffer_8_out, NOR2);
  and and_6 (and_6_out, ~NOR3, NAND3);  // AND_Gate
  and and_7 (and_7_out, Ncin, NAND1, NAND2, NAND3);
  and and_8 (and_8_out, NAND3, NAND2, NOR1);
  and and_9 (and_9_out, NAND3, NOR2);
  buf buffer_9 (buffer_9_out, NOR3);
  and and_10 (and_10_out, ~NOR4, NAND4);  // AND_Gate
  and and_11 (and_11_out, NAND4, Ncin, NAND1, NAND2, NAND3);
  and and_12 (and_12_out, NOR1, NAND4, NAND3, NAND2);
  and and_13 (and_13_out, NAND4, NAND3, NOR2);
  and and_14 (and_14_out, NOR3, NAND4);
  buf buffer_10 (buffer_10_out, NOR4);
  nor nor_5 (nor_5_out, and_2_out, buffer_7_out);
  nor nor_6 (nor_6_out, and_4_out, and_5_out, buffer_8_out);
  nor nor_7 (nor_7_out, and_7_out, and_8_out, and_9_out, buffer_9_out);
  nor nor_8 (nor_8_out, and_11_out, and_12_out, and_13_out, and_14_out, buffer_10_out);
  xor xor_1 (xor_1_out, not_2_out, and_1_out);
  xor xor_2 (xor_2_out, nor_5_out, and_3_out);
  xor xor_3 (xor_3_out, nor_6_out, and_6_out);
  xor xor_4 (xor_4_out, nor_7_out, and_10_out);
  buf buffer_11 (Sum_Out[0], xor_1_out);
  // Probe on Sum_Out[0]
  // Probe on Sum_Out[1]
  buf buffer_12 (Sum_Out[1], xor_2_out);
  // Probe on Sum_Out[2]
  buf buffer_13 (Sum_Out[2], xor_3_out);
  // Probe on Sum_Out[3]
  buf buffer_14 (Sum_Out[3], xor_4_out);
  // Probe on Carry_Out
  buf buffer_15 (Carry_Out, nor_8_out);

  // Other names for the same wires on the sheet: A[3:0] = Ain; A1 = Ain[0]; A2 = Ain[1]; A3 = Ain[2]; A4 = Ain[3];
  //   B[3:0] = Bin; B1 = Bin[0]; B2 = Bin[1]; B3 = Bin[2]; B4 = Bin[3]; C3 = Carry_Out; Cin = Cinin;
  //   Sum[3:0] = Sum_Out
endmodule
