// Logisim project bitcounter.circ as structural Verilog: 1 circuit, main circuit implementation
module implementation (
  input  [7:0] BitsIn,
  input  CountZerosIn,
  output [3:0] BitCountOut
);

  wire adder_1_cout, adder_1_out, adder_2_cout, adder_2_out, adder_3_cout, adder_3_out, adder_4_cout,
       adder_4_out, adder_5_cout, adder_5_out, adder_6_cout, adder_6_out, adder_7_cout, adder_7_out,
       adder_8_cout, adder_8_out, adder_9_cout, adder_10_cout, adder_11_cout, adder_12_cout, adder_13_cout,
       adder_14_cout;
  wire [1:0] adder_9_out, adder_10_out, adder_11_out, adder_12_out, bit_extender_1_out, bit_extender_2_out,
       bit_extender_3_out, bit_extender_4_out, bit_extender_5_out, bit_extender_6_out, bit_extender_7_out,
       bit_extender_8_out;
  wire [2:0] adder_13_out, adder_14_out, bit_extender_9_out, bit_extender_10_out, bit_extender_11_out,
       bit_extender_12_out;
  wire [3:0] bit_extender_13_out, bit_extender_14_out;
  wire [7:0] demultiplexer_1_out0, demultiplexer_1_out1, not_1_out;

  Demultiplexer #(.enable("false"), .width(8)) demultiplexer_1 (
    .out0(demultiplexer_1_out0), .out1(demultiplexer_1_out1), .in(BitsIn), .sel(CountZerosIn));
  // Probe on demultiplexer_1_out0
  assign not_1_out = ~demultiplexer_1_out1;  // NOT_Gate not_1, 8 bits wide
  // Probe on demultiplexer_1_out1
  Adder #(.width(1)) adder_1 (
    .a(demultiplexer_1_out0[0]), .b(demultiplexer_1_out0[1]), .out(adder_1_out), .cout(adder_1_cout));  // open: cin
  Adder #(.width(1)) adder_2 (.a(not_1_out[0]), .b(not_1_out[1]), .out(adder_2_out), .cout(adder_2_cout));  // open: cin
  Adder #(.width(1)) adder_3 (.a(not_1_out[2]), .b(not_1_out[3]), .out(adder_3_out), .cout(adder_3_cout));  // open: cin
  assign bit_extender_1_out = {{1{adder_1_cout}}, adder_1_out};  // Bit_Extender bit_extender_1
  assign bit_extender_2_out = {{1{adder_4_cout}}, adder_4_out};  // Bit_Extender bit_extender_2
  Adder #(.width(1)) adder_4 (
    .a(demultiplexer_1_out0[2]), .b(demultiplexer_1_out0[3]), .out(adder_4_out), .cout(adder_4_cout));  // open: cin
  Adder #(.width(1)) adder_5 (
    .a(demultiplexer_1_out0[4]), .b(demultiplexer_1_out0[5]), .out(adder_5_out), .cout(adder_5_cout));  // open: cin
  Adder #(.width(1)) adder_6 (
    .a(demultiplexer_1_out0[6]), .b(demultiplexer_1_out0[7]), .out(adder_6_out), .cout(adder_6_cout));  // open: cin
  assign bit_extender_3_out = {{1{adder_2_cout}}, adder_2_out};  // Bit_Extender bit_extender_3
  // Probe on bit_extender_4_out
  assign bit_extender_4_out = {{1{adder_3_cout}}, adder_3_out};  // Bit_Extender bit_extender_4
  assign bit_extender_5_out = {{1{adder_7_cout}}, adder_7_out};  // Bit_Extender bit_extender_5
  Adder #(.width(1)) adder_7 (.a(not_1_out[4]), .b(not_1_out[5]), .out(adder_7_out), .cout(adder_7_cout));  // open: cin
  Adder #(.width(1)) adder_8 (.a(not_1_out[6]), .b(not_1_out[7]), .out(adder_8_out), .cout(adder_8_cout));  // open: cin
  // Probe on bit_extender_1_out
  // Probe on bit_extender_2_out
  // Probe on bit_extender_6_out
  assign bit_extender_6_out = {{1{adder_5_cout}}, adder_5_out};  // Bit_Extender bit_extender_6
  assign bit_extender_7_out = {{1{adder_6_cout}}, adder_6_out};  // Bit_Extender bit_extender_7
  // Probe on bit_extender_7_out
  // Probe on bit_extender_3_out
  // Probe on bit_extender_5_out
  assign bit_extender_8_out = {{1{adder_8_cout}}, adder_8_out};  // Bit_Extender bit_extender_8
  Adder #(.width(2)) adder_9 (
    .a(bit_extender_1_out), .b(bit_extender_2_out), .out(adder_9_out), .cout(adder_9_cout));  // open: cin
  Adder #(.width(2)) adder_10 (
    .a(bit_extender_6_out), .b(bit_extender_7_out), .out(adder_10_out), .cout(adder_10_cout));  // open: cin
  // Probe on adder_11_out
  Adder #(.width(2)) adder_11 (
    .a(bit_extender_3_out), .b(bit_extender_4_out), .out(adder_11_out), .cout(adder_11_cout));  // open: cin
  Adder #(.width(2)) adder_12 (
    .a(bit_extender_5_out), .b(bit_extender_8_out), .out(adder_12_out), .cout(adder_12_cout));  // open: cin
  // Probe on adder_9_out
  assign bit_extender_9_out = {{1{adder_9_cout}}, adder_9_out};  // Bit_Extender bit_extender_9
  assign bit_extender_10_out = {{1{adder_10_cout}}, adder_10_out};  // Bit_Extender bit_extender_10
  assign bit_extender_11_out = {{1{adder_11_cout}}, adder_11_out};  // Bit_Extender bit_extender_11
  assign bit_extender_12_out = {{1{adder_12_cout}}, adder_12_out};  // Bit_Extender bit_extender_12
  Adder #(.width(3)) adder_13 (
    .a(bit_extender_9_out), .b(bit_extender_10_out), .out(adder_13_out), .cout(adder_13_cout));  // open: cin
  Adder #(.width(3)) adder_14 (
    .a(bit_extender_11_out), .b(bit_extender_12_out), .out(adder_14_out), .cout(adder_14_cout));  // open: cin
  assign bit_extender_13_out = {{1{adder_14_cout}}, adder_14_out};  // Bit_Extender bit_extender_13
  assign bit_extender_14_out = {{1{adder_13_cout}}, adder_13_out};  // Bit_Extender bit_extender_14
  Multiplexer #(.enable("false"), .width(4)) multiplexer_1 (
    .in0(bit_extender_14_out), .in1(bit_extender_13_out), .out(BitCountOut), .sel(CountZerosIn));

  // Other names for the same wires on the sheet: BitCount[3:0] = BitCountOut; Bits[7:0] = BitsIn;
  //   CountZeros = CountZerosIn
endmodule
