// Logisim project shifter.circ as structural Verilog: 1 circuit, main circuit implementation
module implementation (
  input  IsRightShiftIn,
  input  IsArithmeticIn,
  input  [1:0] ShiftAmountIn,
  input  [2:0] NumberIn,
  output [2:0] ShiftedNumberOut
);

  wire [2:0] ArithShift, multiplexer_1_out, multiplexer_2_out, multiplexer_3_out, multiplexer_4_out,
       multiplexer_5_out;

  Multiplexer #(.enable("false"), .select(2), .width(3)) multiplexer_1 (
    .in0(NumberIn), .in1({NumberIn[1:0], 1'b0}), .in2({NumberIn[0], 2'b00}), .in3(3'b000),
    .out(multiplexer_1_out), .sel(ShiftAmountIn));
  Multiplexer #(.enable("false"), .select(2), .width(3)) multiplexer_2 (
    .in0(NumberIn), .in1({1'b0, NumberIn[2:1]}), .in2({2'b00, NumberIn[2]}), .in3(3'b000),
    .out(multiplexer_2_out), .sel(ShiftAmountIn));
  // Probe on multiplexer_1_out
  // Probe on multiplexer_2_out
  // Probe on multiplexer_3_out
  Multiplexer #(.enable("false"), .width(3)) multiplexer_3 (
    .in0(multiplexer_1_out), .in1(multiplexer_2_out), .out(multiplexer_3_out), .sel(IsRightShiftIn));
  Multiplexer #(.enable("false"), .width(3)) multiplexer_4 (
    .in0(multiplexer_2_out), .in1({NumberIn[2], multiplexer_2_out[1:0]}), .out(multiplexer_4_out),
    .sel(IsArithmeticIn));
  Multiplexer #(.enable("false"), .width(3)) multiplexer_5 (
    .in0(multiplexer_4_out), .in1(ArithShift), .out(multiplexer_5_out), .sel(IsArithmeticIn));
  // Probe on multiplexer_4_out
  // Probe on ShiftedNumberOut
  Multiplexer #(.enable("false"), .width(3)) multiplexer_6 (
    .in0(multiplexer_3_out), .in1(multiplexer_5_out), .out(ShiftedNumberOut), .sel(IsRightShiftIn));
  // Probe on {3{multiplexer_4_out[2]}}
  Multiplexer #(.enable("false"), .select(2), .width(3)) multiplexer_7 (
    .in0(NumberIn), .in1(multiplexer_4_out), .in2({3{multiplexer_4_out[2]}}),
    .in3({3{multiplexer_4_out[2]}}), .out(ArithShift), .sel(ShiftAmountIn));

  // Other names for the same wires on the sheet: Number[2:0] = NumberIn; IsArithmetic = IsArithmeticIn;
  //   IsRightShift = IsRightShiftIn; ShiftAmount[1:0] = ShiftAmountIn; ShiftedNumber[2:0] = ShiftedNumberOut
endmodule
