// Logisim project FourBitParity.circ as structural Verilog: 2 circuits, main circuit implementation
module implementation (
  input  EnableIn,
  input  InputBitIn,
  input  ClkIn,
  output IsEvenOut
);

  wire [2:0] register_1_q, state_1_x0par;

  Register #(.width(3)) register_1 (.D(state_1_x0par), .en(EnableIn), .clk(ClkIn), .Q(register_1_q));  // open: clr
  state state_1 (
    .x0(register_1_q[0]), .x1(register_1_q[1]), .x2(register_1_q[2]), .in(InputBitIn),
    .x0par(state_1_x0par[0]), .x1par(state_1_x0par[1]), .x2par(state_1_x0par[2]), .out(IsEvenOut));

  // Other names for the same wires on the sheet: Clk = ClkIn; Enable = EnableIn; InputBit = InputBitIn
endmodule

module state (
  input  x0,
  input  x1,
  input  x2,
  input  in,
  output x0par,
  output x1par,
  output x2par,
  output out
);

  wire and_1_out, and_2_out, and_3_out, and_4_out, and_5_out, and_6_out, and_7_out, and_8_out, and_9_out,
       and_10_out, and_11_out, not_1_out, not_2_out, not_3_out, not_4_out, not_5_out, not_6_out, not_7_out,
       not_8_out, not_9_out, not_10_out, not_11_out, not_12_out, not_13_out, not_14_out, not_15_out,
       not_16_out, not_17_out, not_18_out;

  not not_1 (not_1_out, x1);
  not not_2 (not_2_out, x2);
  not not_3 (not_3_out, x2);
  not not_4 (not_4_out, x1);
  not not_5 (not_5_out, x0);
  not not_6 (not_6_out, in);
  not not_7 (not_7_out, x0);
  not not_8 (not_8_out, x1);
  not not_9 (not_9_out, in);
  not not_10 (not_10_out, x0);
  not not_11 (not_11_out, x2);
  not not_12 (not_12_out, x0);
  not not_13 (not_13_out, in);
  not not_14 (not_14_out, x2);
  not not_15 (not_15_out, x1);
  not not_16 (not_16_out, x2);
  and and_1 (and_1_out, x1, not_17_out);
  not not_17 (not_17_out, in);
  and and_2 (and_2_out, not_1_out, x2, in);
  and and_3 (and_3_out, x1, x2, not_18_out);
  not not_18 (not_18_out, x0);
  and and_4 (and_4_out, x1, x0, not_2_out);
  and and_5 (and_5_out, not_3_out, in);
  and and_6 (and_6_out, not_4_out, x2, not_5_out);
  and and_7 (and_7_out, x1, not_6_out, not_7_out);
  and and_8 (and_8_out, not_8_out, not_9_out, not_10_out);
  and and_9 (and_9_out, not_11_out, in, x1);
  and and_10 (and_10_out, not_12_out, x1, x2);
  and and_11 (and_11_out, x0, not_13_out, not_14_out);
  and and_12 (out, not_15_out, x0, not_16_out);
  or or_1 (x0par, and_1_out, and_2_out, and_3_out, and_4_out);
  or or_2 (x1par, and_5_out, and_6_out, and_7_out);
  or or_3 (x2par, and_8_out, and_9_out, and_10_out, and_11_out);

  // Other names for the same wires on the sheet: inp = in
endmodule
