// Logisim project UpDownCounter.circ as structural Verilog: 2 circuits, main circuit implementation
module implementation (
  input  EnableIn,
  input  CountUpIn,
  input  CountDownIn,
  input  clkIn,
  output [2:0] Count
);

  wire [2:0] next_state_1_next_st;

  next_state next_state_1 (
    .current_st(Count), .EnableIn(EnableIn), .UpIn(CountUpIn), .DownIn(CountDownIn),
    .next_st(next_state_1_next_st));
  Register #(.width(3)) register_1 (.D(next_state_1_next_st), .clk(clkIn), .Q(Count));  // open: en, clr
  // Probe on Count

  // Other names for the same wires on the sheet: clk = clkIn; CountDown = CountDownIn; CountUp = CountUpIn;
  //   Enable = EnableIn; State[2:0] = Count
endmodule

module next_state (
  input  [2:0] current_st,
  input  EnableIn,
  input  UpIn,
  input  DownIn,
  output [2:0] next_st
);

  wire and_1_out, and_2_out, and_3_out, and_4_out, and_5_out, and_6_out, and_7_out, and_8_out, and_9_out,
       and_10_out, and_11_out, and_12_out, and_13_out, and_14_out, and_15_out, and_16_out, and_17_out,
       not_1_out, not_2_out, not_3_out, not_4_out, not_5_out;

  not not_1 (not_1_out, current_st[1]);
  not not_2 (not_2_out, current_st[0]);
  not not_3 (not_3_out, EnableIn);
  not not_4 (not_4_out, UpIn);
  not not_5 (not_5_out, DownIn);
  and and_1 (and_1_out, current_st[1], current_st[0], EnableIn, UpIn, not_5_out);
  and and_2 (and_2_out, current_st[2], not_3_out);
  and and_3 (and_3_out, current_st[2], not_5_out);
  and and_4 (and_4_out, current_st[2], current_st[0], not_4_out);
  and and_5 (and_5_out, current_st[2], current_st[1], not_4_out);
  and and_6 (and_6_out, not_1_out, current_st[0], EnableIn, UpIn);
  and and_7 (and_7_out, current_st[1], not_2_out, not_5_out);
  and and_8 (and_8_out, current_st[1], not_3_out);
  and and_9 (and_9_out, current_st[1], current_st[0], not_4_out);
  and and_10 (and_10_out, current_st[2], not_1_out, not_2_out, EnableIn, DownIn);
  and and_11 (and_11_out, current_st[2], current_st[1], not_5_out);
  and and_12 (and_12_out, not_2_out, EnableIn, UpIn);
  and and_13 (and_13_out, current_st[0], not_3_out);
  and and_14 (and_14_out, current_st[0], not_4_out, not_5_out);
  and and_15 (and_15_out, current_st[1], not_2_out, EnableIn, DownIn);
  and and_16 (and_16_out, current_st[2], not_2_out, EnableIn, DownIn);
  and and_17 (and_17_out, current_st[2], current_st[1], current_st[0], UpIn);
  or or_1 (next_st[2], and_1_out, and_2_out, and_3_out, and_4_out, and_5_out);
  or or_2 (next_st[1], and_6_out, and_7_out, and_8_out, and_9_out, and_10_out, and_11_out);
  or or_3 (next_st[0], and_12_out, and_13_out, and_14_out, and_15_out, and_16_out, and_17_out);
endmodule
