// Logisim project Vending.circ as structural Verilog: 3 circuits, main circuit implementation
module implementation (
  input  EnableIn,
  input  QuarterReceivedIn,
  input  DimeReceivedIn,
  input  NickelReceivedIn,
  input  ClkIn,
  output Give_Mechandise_Out,
  output Give_Dime_Out,
  output Give_Nickel_Out
);

  wire [2:0] next_state_1_nextstate, register_1_q;

  Next_State next_state_1 (
    .CurrentStates(register_1_q), .QuarterIn(QuarterReceivedIn), .DimeIn(DimeReceivedIn),
    .NickleIn(NickelReceivedIn), .NextState(next_state_1_nextstate));
  // Probe on register_1_q
  Register #(.width(3)) register_1 (
    .D(next_state_1_nextstate), .en(EnableIn), .clk(ClkIn), .Q(register_1_q));  // open: clr
  Output_Logic output_logic_1 (
    .CurrentStates(register_1_q), .QuarterIn(QuarterReceivedIn), .DimeIn(DimeReceivedIn),
    .NickleIn(NickelReceivedIn), .Merch(Give_Mechandise_Out), .Dime_ch(Give_Dime_Out),
    .Nickle_ch(Give_Nickel_Out));

  // Other names for the same wires on the sheet: clk = ClkIn; DimeReceieved = DimeReceivedIn; Enable = EnableIn;
  //   Give_Dime = Give_Dime_Out; Give_Merchandise = Give_Mechandise_Out; Give_Nickel = Give_Nickel_Out;
  //   NickelReceieved = NickelReceivedIn; QuarterReceieved = QuarterReceivedIn
endmodule

module Next_State (
  input  [2:0] CurrentStates,
  input  QuarterIn,
  input  DimeIn,
  input  NickleIn,
  output [2:0] NextState
);

  wire and_1_out, and_2_out, and_3_out, and_4_out, and_5_out, and_6_out, and_7_out, and_8_out, and_9_out,
       and_10_out, and_11_out, and_12_out, and_13_out, and_14_out, and_15_out, and_16_out, and_17_out,
       and_18_out, and_19_out, and_20_out, and_21_out, and_22_out, and_23_out, and_24_out, and_25_out,
       not_1_out, not_2_out, not_3_out, not_4_out, not_5_out, not_6_out;

  not not_1 (not_1_out, CurrentStates[2]);
  not not_2 (not_2_out, CurrentStates[1]);
  not not_3 (not_3_out, CurrentStates[0]);
  not not_4 (not_4_out, QuarterIn);
  not not_5 (not_5_out, DimeIn);
  not not_6 (not_6_out, NickleIn);
  and and_1 (and_1_out, CurrentStates[1], not_4_out, DimeIn, not_6_out);
  and and_2 (and_2_out, CurrentStates[1], CurrentStates[0], not_4_out, not_5_out, NickleIn);
  and and_3 (and_3_out, CurrentStates[2], not_4_out, not_5_out, not_6_out);
  and and_4 (and_4_out, CurrentStates[2], not_3_out, NickleIn);
  and and_5 (and_5_out, CurrentStates[2], DimeIn, NickleIn);
  and and_6 (and_6_out, CurrentStates[2], QuarterIn, NickleIn);
  and and_7 (and_7_out, CurrentStates[2], QuarterIn, DimeIn);
  and and_8 (and_8_out, CurrentStates[2], CurrentStates[1]);
  and and_9 (and_9_out, not_1_out, not_3_out, not_4_out, not_5_out, NickleIn);
  and and_10 (and_10_out, not_1_out, not_2_out, not_3_out, not_4_out, DimeIn, not_6_out);
  and and_11 (and_11_out, CurrentStates[1], not_4_out, not_5_out, not_6_out);
  and and_12 (and_12_out, CurrentStates[1], DimeIn, NickleIn);
  and and_13 (and_13_out, CurrentStates[1], QuarterIn, NickleIn);
  and and_14 (and_14_out, CurrentStates[1], QuarterIn, DimeIn);
  and and_15 (and_15_out, CurrentStates[2], CurrentStates[1]);
  and and_16 (and_16_out, not_2_out, not_3_out, not_4_out, DimeIn, not_6_out);
  and and_17 (and_17_out, not_1_out, not_2_out, not_3_out, QuarterIn, not_5_out, not_6_out);
  and and_18 (and_18_out, CurrentStates[0], not_4_out, not_5_out, not_6_out);
  and and_19 (and_19_out, CurrentStates[0], DimeIn, NickleIn);
  and and_20 (and_20_out, CurrentStates[0], QuarterIn, NickleIn);
  and and_21 (and_21_out, CurrentStates[0], QuarterIn, DimeIn);
  and and_22 (and_22_out, not_1_out, CurrentStates[1], not_3_out, not_4_out, not_5_out, NickleIn);
  and and_23 (and_23_out, CurrentStates[1], CurrentStates[0], DimeIn);
  and and_24 (and_24_out, CurrentStates[2], not_2_out, not_4_out, not_5_out, NickleIn);
  and and_25 (and_25_out, CurrentStates[2], CurrentStates[1], CurrentStates[0]);
  or or_1 (NextState[2], and_1_out, and_2_out, and_3_out, and_4_out, and_5_out, and_6_out, and_7_out, and_8_out);
  or or_2 (NextState[1], and_9_out, and_10_out, and_11_out, and_12_out, and_13_out, and_14_out, and_15_out);
  or or_3 (NextState[0], and_16_out, and_17_out, and_18_out, and_19_out, and_20_out, and_21_out, and_22_out, and_23_out, and_24_out, and_25_out);
endmodule

module Output_Logic (
  input  [2:0] CurrentStates,
  input  QuarterIn,
  input  DimeIn,
  input  NickleIn,
  output Merch,
  output Dime_ch,
  output Nickle_ch
);

  wire and_1_out, and_2_out, and_3_out, and_4_out, and_5_out, and_6_out, and_7_out, and_8_out, and_9_out,
       and_10_out, not_1_out, not_2_out, not_3_out, not_4_out, not_5_out;

  not not_1 (not_1_out, CurrentStates[2]);
  not not_2 (not_2_out, CurrentStates[1]);
  not not_3 (not_3_out, QuarterIn);
  not not_4 (not_4_out, DimeIn);
  not not_5 (not_5_out, NickleIn);
  and and_1 (and_1_out, not_1_out, not_2_out, CurrentStates[0], not_3_out, not_4_out, NickleIn);
  and and_2 (and_2_out, not_2_out, CurrentStates[0], not_3_out, DimeIn, not_5_out);
  and and_3 (and_3_out, not_1_out, CurrentStates[0], QuarterIn, not_4_out, not_5_out);
  and and_4 (and_4_out, not_1_out, CurrentStates[1], QuarterIn, not_4_out, not_5_out);
  and and_5 (and_5_out, CurrentStates[2], not_2_out, QuarterIn, not_4_out, not_5_out);
  and and_6 (and_6_out, not_2_out, CurrentStates[0], QuarterIn, not_4_out, not_5_out);
  and and_7 (and_7_out, CurrentStates[2], not_2_out, QuarterIn, not_4_out, not_5_out);
  and and_8 (and_8_out, not_1_out, not_2_out, CurrentStates[0], not_3_out, DimeIn, not_5_out);
  and and_9 (and_9_out, not_1_out, CurrentStates[0], QuarterIn, not_4_out, not_5_out);
  and and_10 (and_10_out, not_2_out, CurrentStates[0], QuarterIn, not_4_out, not_5_out);
  or or_1 (Merch, and_1_out, and_2_out, and_3_out, and_4_out, and_5_out);
  or or_2 (Dime_ch, and_6_out, and_7_out);
  or or_3 (Nickle_ch, and_8_out, and_9_out, and_10_out);
endmodule
