// Logisim project CPU.circ as structural Verilog: 4 circuits, main circuit implementation
module implementation (
  input  [15:0] Instruction_In,
  input  ClkIn,
  output [4:0] Instruction_Address_Out,
  output [3:0] Reg0_Out,
  output [3:0] Reg1_Out,
  output [3:0] Reg2_Out,
  output [3:0] Reg3_Out,
  output [3:0] Reg4_Out,
  output [3:0] Reg5_Out,
  output [3:0] Reg6_Out,
  output [3:0] Reg7_Out,
  output [3:0] Reg8_Out,
  output [3:0] Reg9_Out,
  output [3:0] Reg10_Out,
  output [3:0] Reg11_Out,
  output [3:0] Reg12_Out,
  output [3:0] Reg13_Out,
  output [3:0] Reg14_Out,
  output [3:0] Reg15_Out
);

  wire and_1_out, Halt, Imm, not_1_out, Reg_write;
  wire [3:0] A_Sel, A_Value, B_Sel, B_Value, C_Sel, multiplexer_1_out, OpCode, Result;

  not not_1 (not_1_out, Halt);
  and and_1 (and_1_out, ClkIn, not_1_out);
  Counter #(.max('h1f), .width(5)) counter_1 (
    .load(and_1_out), .clk(ClkIn), .Q(Instruction_Address_Out));  // open: clr, up, count, D, carry
  InstructionDecoder instructiondecoder_1 (
    .Instructions(Instruction_In), .srcA_1Reg(A_Sel), .srcB_2Reg_imm(B_Sel), .destC_Reg(C_Sel),
    .OpCode(OpCode), .Write_Data(Reg_write), .Immediate(Imm), .Halt(Halt));  // open: Nop
  // Probe on Instruction_Address_Out
  // Probe on A_Sel
  // Probe on B_Sel
  // Probe on C_Sel
  // Probe on A_Value
  RegFile regfile_1 (
    .A_Sel_In(A_Sel), .B_Sel_In(B_Sel), .C_Sel_In(C_Sel), .Data_In(Result), .Reg_Write_In(Reg_write),
    .clk_in(ClkIn), .A_Out(A_Value), .B_Out(B_Value), .Reg0_Out(Reg0_Out), .Reg1_Out(Reg1_Out),
    .Reg2_Out(Reg2_Out), .Reg3_Out(Reg3_Out), .Reg4_Out(Reg4_Out), .Reg5_Out(Reg5_Out), .Reg6_Out(Reg6_Out),
    .Reg7_Out(Reg7_Out), .Reg8_Out(Reg8_Out), .Reg9_Out(Reg9_Out), .Reg10_Out(Reg10_Out),
    .Reg11_Out(Reg11_Out), .Reg12_Out(Reg12_Out), .Reg13_Out(Reg13_Out), .Reg14_Out(Reg14_Out),
    .Reg15_Out(Reg15_Out));
  // Probe on B_Value
  Multiplexer #(.enable("false"), .width(4)) multiplexer_1 (
    .in0(B_Value), .in1(B_Sel), .out(multiplexer_1_out), .sel(Imm));
  // Probe on Result
  ALU alu_1 (.A(A_Value), .B(multiplexer_1_out), .OpCode(OpCode), .ALU_Result(Result));

  // Other names for the same wires on the sheet: Clk = ClkIn; Instruction[15:0] = Instruction_In;
  //   Instruction_Address[4:0] = Instruction_Address_Out; Reg0[3:0] = Reg0_Out; Reg1[3:0] = Reg1_Out;
  //   Reg2[3:0] = Reg2_Out; Reg3[3:0] = Reg3_Out; Reg4[3:0] = Reg4_Out; Reg5[3:0] = Reg5_Out; Reg6[3:0] = Reg6_Out;
  //   Reg7[3:0] = Reg7_Out; Reg8[3:0] = Reg8_Out; Reg9[3:0] = Reg9_Out; Reg10[3:0] = Reg10_Out;
  //   Reg11[3:0] = Reg11_Out; Reg12[3:0] = Reg12_Out; Reg13[3:0] = Reg13_Out; Reg14[3:0] = Reg14_Out;
  //   Reg15[3:0] = Reg15_Out
endmodule

module RegFile (
  input  [3:0] A_Sel_In,
  input  [3:0] B_Sel_In,
  input  [3:0] C_Sel_In,
  input  [3:0] Data_In,
  input  Reg_Write_In,
  input  clk_in,
  output [3:0] A_Out,
  output [3:0] B_Out,
  output [3:0] Reg0_Out,
  output [3:0] Reg1_Out,
  output [3:0] Reg2_Out,
  output [3:0] Reg3_Out,
  output [3:0] Reg4_Out,
  output [3:0] Reg5_Out,
  output [3:0] Reg6_Out,
  output [3:0] Reg7_Out,
  output [3:0] Reg8_Out,
  output [3:0] Reg9_Out,
  output [3:0] Reg10_Out,
  output [3:0] Reg11_Out,
  output [3:0] Reg12_Out,
  output [3:0] Reg13_Out,
  output [3:0] Reg14_Out,
  output [3:0] Reg15_Out
);

  wire Reg_Write0, Reg_Write1, Reg_Write2, Reg_Write3, Reg_Write4, Reg_Write5, Reg_Write6, Reg_Write7,
       Reg_Write8, Reg_Write9, Reg_Write10, Reg_Write11, Reg_Write12, Reg_Write13, Reg_Write14, Reg_Write15;

  Demultiplexer #(.enable("false"), .select(4)) demultiplexer_1 (
    .out0(Reg_Write0), .out1(Reg_Write1), .out2(Reg_Write2), .out3(Reg_Write3), .out4(Reg_Write4),
    .out5(Reg_Write5), .out6(Reg_Write6), .out7(Reg_Write7), .out8(Reg_Write8), .out9(Reg_Write9),
    .out10(Reg_Write10), .out11(Reg_Write11), .out12(Reg_Write12), .out13(Reg_Write13), .out14(Reg_Write14),
    .out15(Reg_Write15), .in(Reg_Write_In), .sel(C_Sel_In));
  Register #(.width(4)) register_1 (.D(Data_In), .en(Reg_Write0), .clk(clk_in), .Q(Reg0_Out));  // open: clr
  Register #(.width(4)) register_2 (.D(Data_In), .en(Reg_Write4), .clk(clk_in), .Q(Reg4_Out));  // open: clr
  Register #(.width(4)) register_3 (.D(Data_In), .en(Reg_Write8), .clk(clk_in), .Q(Reg8_Out));  // open: clr
  Register #(.width(4)) register_4 (.D(Data_In), .en(Reg_Write12), .clk(clk_in), .Q(Reg12_Out));  // open: clr
  Register #(.width(4)) register_5 (.D(Data_In), .en(Reg_Write1), .clk(clk_in), .Q(Reg1_Out));  // open: clr
  Register #(.width(4)) register_6 (.D(Data_In), .en(Reg_Write5), .clk(clk_in), .Q(Reg5_Out));  // open: clr
  Register #(.width(4)) register_7 (.D(Data_In), .en(Reg_Write9), .clk(clk_in), .Q(Reg9_Out));  // open: clr
  Register #(.width(4)) register_8 (.D(Data_In), .en(Reg_Write13), .clk(clk_in), .Q(Reg13_Out));  // open: clr
  Register #(.width(4)) register_9 (.D(Data_In), .en(Reg_Write2), .clk(clk_in), .Q(Reg2_Out));  // open: clr
  Register #(.width(4)) register_10 (.D(Data_In), .en(Reg_Write6), .clk(clk_in), .Q(Reg6_Out));  // open: clr
  Register #(.width(4)) register_11 (.D(Data_In), .en(Reg_Write10), .clk(clk_in), .Q(Reg10_Out));  // open: clr
  Register #(.width(4)) register_12 (.D(Data_In), .en(Reg_Write14), .clk(clk_in), .Q(Reg14_Out));  // open: clr
  Register #(.width(4)) register_13 (.D(Data_In), .en(Reg_Write3), .clk(clk_in), .Q(Reg3_Out));  // open: clr
  Register #(.width(4)) register_14 (.D(Data_In), .en(Reg_Write7), .clk(clk_in), .Q(Reg7_Out));  // open: clr
  Register #(.width(4)) register_15 (.D(Data_In), .en(Reg_Write11), .clk(clk_in), .Q(Reg11_Out));  // open: clr
  Register #(.width(4)) register_16 (.D(Data_In), .en(Reg_Write15), .clk(clk_in), .Q(Reg15_Out));  // open: clr
  Multiplexer #(.enable("false"), .select(4), .width(4)) multiplexer_1 (
    .in0(Reg0_Out), .in1(Reg1_Out), .in2(Reg2_Out), .in3(Reg3_Out), .in4(Reg4_Out), .in5(Reg5_Out),
    .in6(Reg6_Out), .in7(Reg7_Out), .in8(Reg8_Out), .in9(Reg9_Out), .in10(Reg10_Out), .in11(Reg11_Out),
    .in12(Reg12_Out), .in13(Reg13_Out), .in14(Reg14_Out), .in15(Reg15_Out), .out(A_Out), .sel(A_Sel_In));
  Multiplexer #(.enable("false"), .select(4), .width(4)) multiplexer_2 (
    .in0(Reg0_Out), .in1(Reg1_Out), .in2(Reg2_Out), .in3(Reg3_Out), .in4(Reg4_Out), .in5(Reg5_Out),
    .in6(Reg6_Out), .in7(Reg7_Out), .in8(Reg8_Out), .in9(Reg9_Out), .in10(Reg10_Out), .in11(Reg11_Out),
    .in12(Reg12_Out), .in13(Reg13_Out), .in14(Reg14_Out), .in15(Reg15_Out), .out(B_Out), .sel(B_Sel_In));

  // Other names for the same wires on the sheet: A[3:0] = A_Out; A_Sel[3:0] = A_Sel_In; B[3:0] = B_Out;
  //   B_Sel[3:0] = B_Sel_In; C_Sel[3:0] = C_Sel_In; clk = clk_in; Data[3:0] = Data_In; Reg0[3:0] = Reg0_Out;
  //   Reg1[3:0] = Reg1_Out; Reg2[3:0] = Reg2_Out; Reg3[3:0] = Reg3_Out; Reg4[3:0] = Reg4_Out; Reg5[3:0] = Reg5_Out;
  //   Reg6[3:0] = Reg6_Out; Reg7[3:0] = Reg7_Out; Reg8[3:0] = Reg8_Out; Reg9[3:0] = Reg9_Out; Reg10[3:0] = Reg10_Out;
  //   Reg11[3:0] = Reg11_Out; Reg12[3:0] = Reg12_Out; Reg13[3:0] = Reg13_Out; Reg14[3:0] = Reg14_Out;
  //   Reg15[3:0] = Reg15_Out; Reg_Write = Reg_Write_In
endmodule

module ALU (
  input  [3:0] A,
  input  [3:0] B,
  input  [3:0] OpCode,
  output [3:0] ALU_Result
);

  wire [3:0] Add_i, Add_r, And_i, And_r, bit_extender_3_out, Negate, Not_a, Or_i, Or_r, Sub_i, Sub_r, Xor_i,
       Xor_r;
  wire [4:0] adder_2_out, and_2_out, ext_A, Immediate, or_2_out, shifter_1_out, subtractor_2_out, xor_2_out;

  // Probe on A
  assign ext_A = {{1{1'b0}}, A};  // Bit_Extender bit_extender_1
  assign Immediate = {{1{1'b0}}, B};  // Bit_Extender bit_extender_2
  // Probe on B
  // Probe on ext_A
  Bit_Extender #(.in_width(5), .out_width(4)) bit_extender_3 (.in(Immediate), .out(bit_extender_3_out));
  // Probe on Immediate
  // Probe on bit_extender_3_out
  assign And_r = A & B;  // AND_Gate and_1, 4 bits wide
  assign Or_r = A | B;  // OR_Gate or_1, 4 bits wide
  assign Xor_r = A ^ B;  // XOR_Gate xor_1, 4 bits wide
  assign Not_a = ~A;  // NOT_Gate not_1, 4 bits wide
  Negator #(.width(4)) negator_1 (.in(A), .out(Negate));
  Adder #(.width(4)) adder_1 (.a(A), .b(B), .out(Add_r));  // open: cin, cout
  Subtractor #(.width(4)) subtractor_1 (.a(A), .b(B), .out(Sub_r));  // open: bin, bout
  assign and_2_out = ext_A & Immediate;  // AND_Gate and_2, 5 bits wide
  assign or_2_out = ext_A | Immediate;  // OR_Gate or_2, 5 bits wide
  assign xor_2_out = ext_A ^ Immediate;  // XOR_Gate xor_2, 5 bits wide
  Adder #(.width(5)) adder_2 (.a(ext_A), .b(Immediate), .out(adder_2_out));  // open: cin, cout
  // Probe on adder_2_out
  Subtractor #(.width(5)) subtractor_2 (.a(ext_A), .b(Immediate), .out(subtractor_2_out));  // open: bin, bout
  // Probe on subtractor_2_out
  Bit_Extender #(.in_width(5), .out_width(4)) bit_extender_4 (.in(and_2_out), .out(And_i));
  // Probe on And_i
  Bit_Extender #(.in_width(5), .out_width(4)) bit_extender_5 (.in(or_2_out), .out(Or_i));
  // Probe on Or_i
  Bit_Extender #(.in_width(5), .out_width(4)) bit_extender_6 (.in(xor_2_out), .out(Xor_i));
  // Probe on Xor_i
  Bit_Extender #(.in_width(5), .out_width(4), .\type ("zero")) bit_extender_7 (.in(adder_2_out), .out(Add_i));
  // Probe on Add_i
  Bit_Extender #(.in_width(5), .out_width(4)) bit_extender_8 (.in(subtractor_2_out), .out(Sub_i));
  // Probe on Sub_i
  // Probe on shifter_1_out
  Shifter #(.width(5)) shifter_1 (.in(subtractor_2_out), .\dist (3'b111), .out(shifter_1_out));
  Multiplexer #(.enable("false"), .select(4), .width(4)) multiplexer_1 (
    .in2(B), .in3(A), .in4(And_r), .in5(And_i), .in6(Or_r), .in7(Or_i), .in8(Xor_r), .in9(Xor_i),
    .in10(Not_a), .in11(Negate), .in12(Add_r), .in13(Add_i), .in14(Sub_r), .in15(Sub_i), .out(ALU_Result),
    .sel(OpCode));  // open: in0, in1
  // Probe on ALU_Result

  // Other names for the same wires on the sheet: Load[3:0] = B; Move[3:0] = A
endmodule

module InstructionDecoder (
  input  [15:0] Instructions,
  output [3:0] srcA_1Reg,
  output [3:0] srcB_2Reg_imm,
  output [3:0] destC_Reg,
  output [3:0] OpCode,
  output Write_Data,
  output Immediate,
  output Halt,
  output Nop
);

  Comparator #(.mode("unsigned"), .width(4)) comparator_1 (
    .a(Instructions[15:12]), .b(4'b0001), .gt(Write_Data));  // open: eq, lt
  // Probe on Instructions[15:12]
  Multiplexer #(.enable("false"), .select(4)) multiplexer_1 (
    .in0(1'b0), .in1(1'b0), .in2(1'b1), .in3(1'b0), .in4(1'b0), .in5(1'b1), .in6(1'b0), .in7(1'b1),
    .in8(1'b0), .in9(1'b1), .in10(1'b0), .in11(1'b0), .in12(1'b0), .in13(1'b1), .in14(1'b0), .in15(1'b1),
    .out(Immediate), .sel(Instructions[15:12]));
  nor nor_1 (Halt, Instructions[12], Instructions[13], Instructions[14], Instructions[15]);
  nor nor_2 (Nop, ~Instructions[12], Instructions[13], Instructions[14], Instructions[15]);  // NOR_Gate

  assign destC_Reg = Instructions[11:8];
  assign OpCode = Instructions[15:12];
  assign srcA_1Reg = Instructions[7:4];
  assign srcB_2Reg_imm = Instructions[3:0];

  // Other names for the same wires on the sheet: B_Immediate[3:0] = Instructions[3:0]; A[3:0] = Instructions[7:4];
  //   C[3:0] = Instructions[11:8]
endmodule
